// Logisim project LC-2200-16.circ as structural Verilog: 5 circuits, main circuit main
module main (
  input  in_1,
  input  [15:0] in_2,
  input  [3:0] in_3,
  input  in_4
);

  wire CLK, comparator_1_eq, comparator_2_eq, DrALU, DrMEM, DrOFF, DrPC, DrREG, LdA, LdB, LdIR, LdMAR, LdPC,
       WrMEM, WrREG, Z;
  wire [1:0] func, RegSel;
  wire [2:0] OP;
  wire [3:0] controlled_buffer_1_out, controlled_buffer_1_out_2, controlled_buffer_1_out_3,
       controlled_buffer_1_out_4, regno, RX, RY;
  wire [4:0] IR4_0;
  wire [10:10] microcontroller_1_control_signals;
  wire [15:0] A_q, ALU_out, B_q, MAR_q, multiplexer_1_out, PC_q, ram_1_data, ram_2_data, SEXT_out;

  Clock clock_1 (.out(CLK));
  Register #(.width(16)) PC (
    .D({controlled_buffer_1_out, controlled_buffer_1_out_2, controlled_buffer_1_out_3, controlled_buffer_1_out_4}),
    .en(LdPC), .Q(PC_q), .clk(CLK));  // open: clr
  assign {controlled_buffer_1_out, controlled_buffer_1_out_2, controlled_buffer_1_out_3, controlled_buffer_1_out_4} = DrPC ? PC_q : 16'bz;  // Controlled_Buffer controlled_buffer_1
  Register #(.width(16)) A (
    .D({controlled_buffer_1_out, controlled_buffer_1_out_2, controlled_buffer_1_out_3, controlled_buffer_1_out_4}),
    .en(LdA), .Q(A_q), .clk(CLK));  // open: clr
  Comparator #(.width(16)) comparator_1 (
    .a({controlled_buffer_1_out, controlled_buffer_1_out_2, controlled_buffer_1_out_3, controlled_buffer_1_out_4}),
    .b({16{1'b0}}), .eq(comparator_1_eq));  // open: gt, lt
  Microcontroller microcontroller_1 (
    .Control_Signals({func, RegSel, WrMEM, WrREG, microcontroller_1_control_signals[10], LdB, LdA, LdMAR, LdIR, LdPC, DrOFF, DrPC, DrALU, DrMEM, DrREG}),
    .CLK(CLK), .IR_15_13(OP), .Z({1'b0, Z}));
  Register #(.width(16)) B (
    .D({controlled_buffer_1_out, controlled_buffer_1_out_2, controlled_buffer_1_out_3, controlled_buffer_1_out_4}),
    .en(LdB), .Q(B_q), .clk(CLK));  // open: clr
  ALU ALU (.func(func), .A(A_q), .B(B_q), .Out(ALU_out));
  assign {controlled_buffer_1_out, controlled_buffer_1_out_2, controlled_buffer_1_out_3, controlled_buffer_1_out_4} = DrALU ? ALU_out : 16'bz;  // Controlled_Buffer controlled_buffer_2
  Register #(.width(1)) u_Z (
    .D(comparator_1_eq), .en(microcontroller_1_control_signals[10]), .Q(Z), .clk(CLK));  // open: clr
  Comparator #(.width(4)) comparator_2 (.a(regno), .b(4'b0000), .eq(comparator_2_eq));  // open: gt, lt
  RAM #(.addrWidth(4), .dataWidth(16), .bus("separate")) ram_1 (
    .addr(regno),
    .din({controlled_buffer_1_out, controlled_buffer_1_out_2, controlled_buffer_1_out_3, controlled_buffer_1_out_4}),
    .data(ram_1_data), .str(WrREG));  // open: sel, clk, ld, clr
  Multiplexer #(.width(16)) multiplexer_1 (
    .in0(ram_1_data), .in1({16{1'b0}}), .out(multiplexer_1_out), .sel(comparator_2_eq));  // open: en
  assign {controlled_buffer_1_out, controlled_buffer_1_out_2, controlled_buffer_1_out_3, controlled_buffer_1_out_4} = DrREG ? multiplexer_1_out : 16'bz;  // Controlled_Buffer controlled_buffer_3
  assign {controlled_buffer_1_out, controlled_buffer_1_out_2, controlled_buffer_1_out_3, controlled_buffer_1_out_4} = in_1 ? in_2 : 16'bz;  // Controlled_Buffer controlled_buffer_4
  Register #(.width(16)) MAR (
    .D({controlled_buffer_1_out, controlled_buffer_1_out_2, controlled_buffer_1_out_3, controlled_buffer_1_out_4}),
    .en(LdMAR), .Q(MAR_q), .clk(CLK));  // open: clr
  assign {controlled_buffer_1_out, controlled_buffer_1_out_2, controlled_buffer_1_out_3, controlled_buffer_1_out_4} = DrMEM ? ram_2_data : 16'bz;  // Controlled_Buffer controlled_buffer_5
  Multiplexer #(.select(2), .width(4)) multiplexer_2 (
    .in0(RX), .in1(RY), .in2({IR4_0[1], IR4_0[2], IR4_0[3], IR4_0[4]}), .out(regno), .sel(RegSel));  // open: in3, en
  RAM #(.addrWidth(16), .dataWidth(16), .bus("separate")) ram_2 (
    .addr(MAR_q),
    .din({controlled_buffer_1_out, controlled_buffer_1_out_2, controlled_buffer_1_out_3, controlled_buffer_1_out_4}),
    .data(ram_2_data), .str(WrMEM), .clk(CLK));  // open: sel, ld, clr
  Hex_Digit_Display hex_digit_display_1 (.value(controlled_buffer_1_out));  // open: dp
  Register #(.width(16)) IR (
    .D({controlled_buffer_1_out, controlled_buffer_1_out_2, controlled_buffer_1_out_3, controlled_buffer_1_out_4}),
    .en(LdIR), .Q({OP, RX, RY, IR4_0}), .clk(CLK));  // open: clr
  Hex_Digit_Display hex_digit_display_2 (.value(controlled_buffer_1_out_2));  // open: dp
  Hex_Digit_Display hex_digit_display_3 (.value(controlled_buffer_1_out_3));  // open: dp
  SEXT SEXT (.in(IR4_0), .out(SEXT_out));
  assign {controlled_buffer_1_out, controlled_buffer_1_out_2, controlled_buffer_1_out_3, controlled_buffer_1_out_4} = DrOFF ? SEXT_out : 16'bz;  // Controlled_Buffer controlled_buffer_6
  Hex_Digit_Display hex_digit_display_4 (.value(controlled_buffer_1_out_4));  // open: dp
  RegFile RegFile (.Regno(in_3), .WrMEM(in_4), .CLK(CLK));  // open: Din, Dout

  // Other names for the same wires on the sheet: RZ[3:0] = {IR4_0[1], IR4_0[2], IR4_0[3], IR4_0[4]}

  // Notes on the sheet:
  //   LdZ
  //   16    15    14    13    12    11    10    9    8    7    6    5    4    3    2    1    0
  //   ALUHi ALULo RegSelHi RegSelLo WrMEM WrReg   LdZ   LdB    LdA    LdMAR  LdIR LdPC DrOFF DrPC DrALU DrMEM DrReg 
endmodule

module ALU (
  input  [15:0] A,
  input  [15:0] B,
  input  [1:0] func,
  output [15:0] Out
);

  wire [15:0] adder_1_out, adder_2_out, nand_1_out, subtractor_1_out;

  Adder #(.width(16)) adder_1 (.a(A), .b(B), .out(adder_1_out));  // open: cin, cout
  assign nand_1_out = ~(A & B);  // NAND_Gate nand_1, 16 bits wide
  Subtractor #(.width(16)) subtractor_1 (.a(A), .b(B), .out(subtractor_1_out));  // open: bin, bout
  Adder #(.width(16)) adder_2 (.a(A), .b(16'h1), .out(adder_2_out));  // open: cin, cout
  Multiplexer #(.select(2), .width(16)) multiplexer_1 (
    .in0(adder_1_out), .in1(nand_1_out), .in2(subtractor_1_out), .in3(adder_2_out), .out(Out), .sel(func));  // open: en
endmodule

module RegFile (
  input  [15:0] Din,
  input  [3:0] Regno,
  input  WrMEM,
  input  CLK,
  output [15:0] Dout
);

  wire [15:0] _6, _7, _9, _10, _11, a0_q, a1_q, a2_q, at_q, demultiplexer_1_out0, demultiplexer_1_out1,
       demultiplexer_1_out2, demultiplexer_1_out3, demultiplexer_1_out4, demultiplexer_1_out5,
       demultiplexer_1_out8, demultiplexer_1_out12, demultiplexer_1_out13, demultiplexer_1_out14,
       demultiplexer_1_out15, fp_q, k0_q, ra_q, s0_q, s1_q, s2_q, sp_q, t0_q, t1_q, t2_q, v0_q, zero_q;

  Demultiplexer #(.select(4), .width(16)) demultiplexer_1 (
    .out0(demultiplexer_1_out0), .out1(demultiplexer_1_out1), .out2(demultiplexer_1_out2),
    .out3(demultiplexer_1_out3), .out4(demultiplexer_1_out4), .out5(demultiplexer_1_out5), .out6(_6),
    .out7(_7), .out8(demultiplexer_1_out8), .out9(_9), .out10(_10), .out11(_11),
    .out12(demultiplexer_1_out12), .out13(demultiplexer_1_out13), .out14(demultiplexer_1_out14),
    .out15(demultiplexer_1_out15), .in(Din), .sel(Regno));  // open: en
  Register #(.width(16)) zero (.D(demultiplexer_1_out0), .en(WrMEM), .Q(zero_q), .clk(CLK), .clr(1'b1));
  Register #(.width(16)) a1 (.D(demultiplexer_1_out4), .en(WrMEM), .Q(a1_q), .clk(CLK));  // open: clr
  Register #(.width(16)) t2 (.D(demultiplexer_1_out8), .en(WrMEM), .Q(t2_q), .clk(CLK));  // open: clr
  Register #(.width(16)) k0 (.D(demultiplexer_1_out12), .en(WrMEM), .Q(k0_q), .clk(CLK));  // open: clr
  Register #(.width(16)) at (.D(demultiplexer_1_out1), .en(WrMEM), .Q(at_q), .clk(CLK));  // open: clr
  Register #(.width(16)) a2 (.D(demultiplexer_1_out5), .en(WrMEM), .Q(a2_q), .clk(CLK));  // open: clr
  Register #(.width(16)) s0 (.D(_9), .en(WrMEM), .Q(s0_q), .clk(CLK));  // open: clr
  Register #(.width(16)) sp (.D(demultiplexer_1_out13), .en(WrMEM), .Q(sp_q), .clk(CLK));  // open: clr
  Register #(.width(16)) v0 (.D(demultiplexer_1_out2), .en(WrMEM), .Q(v0_q), .clk(CLK));  // open: clr
  Register #(.width(16)) t0 (.D(_6), .en(WrMEM), .Q(t0_q), .clk(CLK));  // open: clr
  Register #(.width(16)) s1 (.D(_10), .en(WrMEM), .Q(s1_q), .clk(CLK));  // open: clr
  Register #(.width(16)) fp (.D(demultiplexer_1_out14), .en(WrMEM), .Q(fp_q), .clk(CLK));  // open: clr
  Register #(.width(16)) a0 (.D(demultiplexer_1_out3), .en(WrMEM), .Q(a0_q), .clk(CLK));  // open: clr
  Register #(.width(16)) t1 (.D(_7), .en(WrMEM), .Q(t1_q), .clk(CLK));  // open: clr
  Register #(.width(16)) s2 (.D(_11), .en(WrMEM), .Q(s2_q), .clk(CLK));  // open: clr
  Register #(.width(16)) ra (.D(demultiplexer_1_out15), .en(WrMEM), .Q(ra_q), .clk(CLK));  // open: clr
  Multiplexer #(.select(4), .width(16)) multiplexer_1 (
    .in0(zero_q), .in1(at_q), .in2(v0_q), .in3(a0_q), .in4(a1_q), .in5(a2_q), .in6(t0_q), .in7(t1_q),
    .in8(t2_q), .in9(s0_q), .in10(s1_q), .in11(s2_q), .in12(k0_q), .in13(sp_q), .in14(fp_q), .in15(ra_q),
    .out(Dout), .sel(Regno));  // open: en

  // Other names for the same wires on the sheet: REG[3:0] = Regno; WE = WrMEM
endmodule

module SEXT (
  input  [4:0] in,
  output [15:0] out
);


  assign out = {{12{in[4]}}, in[3:0]};
endmodule

module Microcontroller (
  input  [2:0] IR_15_13,
  input  [1:0] Z,
  input  CLK,
  output [16:0] Control_Signals
);

  wire [5:0] multiplexer_1_out, rom_2_data, rom_3_data, State_Register_q;
  wire [24:0] rom_1_data;

  Register #(.width(6)) State_Register (
    .D(multiplexer_1_out), .en(1'b1), .Q(State_Register_q), .clk(CLK));  // open: clr
  ROM #(.addrWidth(6), .dataWidth(25)) rom_1 (
    .addr(State_Register_q), .data({rom_1_data[24:23], Control_Signals, rom_1_data[5:0]}));  // open: sel
  Multiplexer #(.select(2), .width(6)) multiplexer_1 (
    .in0(rom_1_data[5:0]), .in1(rom_2_data), .in2(rom_3_data), .out(multiplexer_1_out),
    .sel(rom_1_data[24:23]));  // open: in3, en
  ROM #(.addrWidth(3), .dataWidth(6)) rom_2 (.addr(IR_15_13), .data(rom_2_data));  // open: sel
  ROM #(.addrWidth(2), .dataWidth(6)) rom_3 (.addr(Z), .data(rom_3_data));  // open: sel

  // Notes on the sheet:
  //   contents of rom_1 (hex, n*v repeats v):
  //   6201 1082 e00900 84044 108045 20100 84047 108048 220100 a020a 840 8404c 840d 210e 20080 84050 8411
  //   2112 40040 84054 8415 20100 4057 88058 410119 1000000 421b 841c 900 1d
  //   contents of rom_2 (hex, n*v repeats v):
  //   3 6 13 b f 16 9 1d
  //   contents of rom_3 (hex, n*v repeats v):
  //   0 1a
  //   16    15    14    13    12    11    10    9    8    7    6    5    4    3    2    1    0
  //   ALUHi ALULo RegSelHi RegSelLo WrMEM WrReg   LdZ   LdB    LdA    LdMAR  LdIR LdPC DrOFF DrPC DrALU DrMEM DrReg 
endmodule
