// Logisim project Pierce_Clayton.circ as structural Verilog: 17 circuits, main circuit main
module main (
);

  wire CLK, CNT_2_ld, CNT_2_str, CNT_mux, comparator_1_eq, FLUSH, forward_circ_1_fy, forward_circ_1_fz,
       or_1_out, Stall1, Stall2, wbcontrol_1_regmux, wbcontrol_1_wren;
  wire [1:0] CNT_func, PCMO, PCMux, wbcontrol_1_mux;
  wire [3:0] ExeOP, ExeRX, IDOP, idrr_ex_buffer_1_ryout, IDRX, IDRY, IDRZ, mem_wb_buffer_1_opout,
       mem_wb_buffer_1_ryout, MEMOP, MEMRx, MEMRy, multiplexer_5_out, R2, WBRx;
  wire [19:4] if_idrr_buffer_1_imout;
  wire [23:0] adder_1_out, adder_2_out, ex_mem_buffer_1_addout, ex_mem_buffer_1_pc_1_2, EXEPC,
       if_idrr_buffer_1_pc_1out, mem_wb_buffer_1_pc_1_2, multiplexer_1_out, PC_q, sred_1_dout, SRED_2_dout,
       SRED_3_dout, undriven;
  wire [31:0] A, B, ex_mem_buffer_1_aluout, ex_mem_buffer_1_datain_2, EXEout, forward_circ_1_fwryout,
       forward_circ_1_fwrzrxout, idrr_ex_buffer_1_aout, idrr_ex_buffer_1_bout, idrr_ex_buffer_1_sexout,
       mem_wb_buffer_1_addrout, mem_wb_buffer_1_datain_2, MEMout, multiplexer_3_out, O1, O2, pcext_1_out_2,
       ram_1_data, SEXT_dout, WBout;

  Register #(.width(24)) PC (.D(multiplexer_1_out), .Q(PC_q), .clk(CLK));  // open: en, clr
  Adder #(.width(24)) adder_1 (.a(PC_q), .b(24'h1), .out(adder_1_out));  // open: cin, cout
  StallCheck stallcheck_1 (
    .PCMuxout(PCMO), .Stall1(Stall1), .Stall2(Stall2), .OPCode(ExeOP), .RX(ExeRX), .RY(IDRY), .RZ(IDRZ),
    .ID_RROP(IDOP), .PCMux(PCMux));
  Clock clock_1 (.out(CLK));
  RAM #(.addrWidth(24), .dataWidth(32)) ram_1 (.addr(PC_q), .data(ram_1_data), .clk(CLK));  // open: sel, ld, clr
  IDRRControl idrrcontrol_1 (.RX(IDRX), .RZ(IDRZ), .OPCode(IDOP), .RX_RZ(R2));
  Multiplexer #(.select(2), .width(24), .enable("false")) multiplexer_1 (
    .in0(adder_1_out), .in1(adder_2_out), .in2(sred_1_dout), .in3(PC_q), .out(multiplexer_1_out), .sel(PCMO));
  IF_IDRR_Buffer if_idrr_buffer_1 (
    .PC_1in(adder_1_out), .IMin(ram_1_data), .CLK(CLK), .CLR(FLUSH), .Stall(Stall1),
    .PC_1out(if_idrr_buffer_1_pc_1out), .IMout({IDOP, IDRX, IDRY, if_idrr_buffer_1_imout, IDRZ}));
  Hex_Digit_Display hex_digit_display_1 (.value(R2));  // open: dp
  SEXT SEXT (.Din({IDOP, IDRX, IDRY, if_idrr_buffer_1_imout, IDRZ}), .Dout(SEXT_dout));
  SRED sred_1 (.Din(idrr_ex_buffer_1_bout), .Dout(sred_1_dout));
  Dual_Ported_Register_File dual_ported_register_file_1 (
    .CLK(CLK), .WrEN(wbcontrol_1_wren), .OUT1(O1), .WrREGNO(multiplexer_5_out), .RdREGNO1(IDRY),
    .RdREGNO2(R2), .OUT2(O2), .INPUT(WBout));
  Forward_Circ forward_circ_1 (
    .RY(IDRY), .RZorRX(R2), .EXERx(ExeRX), .MEMRx(MEMRx), .ExeOut(EXEout), .MemOut(MEMout), .WBRx(WBRx),
    .WBOut(WBout), .FWRYOut(forward_circ_1_fwryout), .FWRZRXOut(forward_circ_1_fwrzrxout),
    .FY(forward_circ_1_fy), .FZ(forward_circ_1_fz));  // open: out_9, out_10
  Multiplexer #(.width(32), .enable("false")) multiplexer_2 (
    .in0(O1), .in1(forward_circ_1_fwryout), .out(A), .sel(forward_circ_1_fy));
  MUXBox muxbox_1 (.Sel(PCMux), .FLUSH(FLUSH), .EQ(comparator_1_eq), .OPCode(ExeOP));
  IDRR_EX_Buffer idrr_ex_buffer_1 (
    .PC_1(if_idrr_buffer_1_pc_1out), .Ain(A), .Bin(B), .SEXin(SEXT_dout), .OPin(IDOP), .RXin(IDRX),
    .RYin(IDRY), .CLK(CLK), .CLR(FLUSH), .in_10(or_1_out), .PC_1out(EXEPC), .Aout(idrr_ex_buffer_1_aout),
    .Bout(idrr_ex_buffer_1_bout), .SEXout(idrr_ex_buffer_1_sexout), .OPout(ExeOP), .RXout(ExeRX),
    .RYout(idrr_ex_buffer_1_ryout));
  or or_1 (or_1_out, 1'b0, Stall2);
  Adder #(.width(24)) adder_2 (.a(EXEPC), .b(SRED_2_dout), .out(adder_2_out));  // open: cin, cout
  SRED SRED_2 (.Din(idrr_ex_buffer_1_sexout), .Dout(SRED_2_dout));
  Multiplexer #(.width(32), .enable("false")) multiplexer_3 (
    .in0(idrr_ex_buffer_1_bout), .in1(idrr_ex_buffer_1_sexout), .out(multiplexer_3_out), .sel(CNT_mux));
  EXControl CNT (.OPCode(ExeOP), .MUX(CNT_mux), .func(CNT_func));
  Multiplexer #(.width(32), .enable("false")) multiplexer_4 (
    .in0(O2), .in1(forward_circ_1_fwrzrxout), .out(B), .sel(forward_circ_1_fz));
  Hex_Digit_Display hex_digit_display_2 (.value(multiplexer_5_out));  // open: dp
  ALU alu_1 (.FUNC(CNT_func), .A(idrr_ex_buffer_1_aout), .B(multiplexer_3_out), .OUT(EXEout));
  Comparator #(.width(32)) comparator_1 (.a({32{1'b0}}), .b(EXEout), .eq(comparator_1_eq));  // open: gt, lt
  Hex_Digit_Display hex_digit_display_3 (.value(WBout[31:28]));  // open: dp
  EX_MEM_Buffer ex_mem_buffer_1 (
    .ADDin(undriven), .ALUin(EXEout), .DATAin(idrr_ex_buffer_1_bout), .OPin(ExeOP), .RXin(ExeRX),
    .RYin(idrr_ex_buffer_1_ryout), .PC_1(EXEPC), .CLK(CLK), .ADDout(ex_mem_buffer_1_addout),
    .ALUout(ex_mem_buffer_1_aluout), .DATAin_2(ex_mem_buffer_1_datain_2), .OPout(MEMOP), .RXout(MEMRx),
    .RYout(MEMRy), .PC_1_2(ex_mem_buffer_1_pc_1_2));
  Hex_Digit_Display hex_digit_display_4 (.value(WBout[23:20]));  // open: dp
  Hex_Digit_Display hex_digit_display_5 (.value(WBout[27:24]));  // open: dp
  SRED SRED_3 (.Din(ex_mem_buffer_1_aluout), .Dout(SRED_3_dout));
  Hex_Digit_Display hex_digit_display_6 (.value(WBout[19:16]));  // open: dp
  MEMControl CNT_2 (.OPCode(MEMOP), .STR(CNT_2_str), .LD(CNT_2_ld));
  Hex_Digit_Display hex_digit_display_7 (.value(WBout[15:12]));  // open: dp
  RAM #(.addrWidth(24), .dataWidth(32), .bus("separate")) ram_2 (
    .addr(SRED_3_dout), .din(ex_mem_buffer_1_datain_2), .data(MEMout), .str(CNT_2_str), .clk(CLK),
    .ld(CNT_2_ld));  // open: sel, clr
  Hex_Digit_Display hex_digit_display_8 (.value(WBout[11:8]));  // open: dp
  Hex_Digit_Display hex_digit_display_9 (.value(WBout[7:4]));  // open: dp
  MEM_WB_Buffer mem_wb_buffer_1 (
    .DATAin(MEMout), .ADDRin(ex_mem_buffer_1_aluout), .OPin(MEMOP), .RXin(MEMRx), .RYin(MEMRy),
    .PC_1(ex_mem_buffer_1_pc_1_2), .CLK(CLK), .DATAin_2(mem_wb_buffer_1_datain_2),
    .ADDRout(mem_wb_buffer_1_addrout), .OPout(mem_wb_buffer_1_opout), .RXout(WBRx),
    .RYout(mem_wb_buffer_1_ryout), .PC_1_2(mem_wb_buffer_1_pc_1_2));
  Multiplexer #(.width(4), .enable("false")) multiplexer_5 (
    .in0(WBRx), .in1(mem_wb_buffer_1_ryout), .out(multiplexer_5_out), .sel(wbcontrol_1_regmux));
  Hex_Digit_Display hex_digit_display_10 (.value(WBout[3:0]));  // open: dp
  PCEXT pcext_1 (.PCin(mem_wb_buffer_1_pc_1_2), .out_2(pcext_1_out_2));
  WBControl wbcontrol_1 (
    .OPCode(mem_wb_buffer_1_opout), .WrEN(wbcontrol_1_wren), .MUX(wbcontrol_1_mux),
    .RegMux(wbcontrol_1_regmux));
  Multiplexer #(.select(2), .width(32), .enable("false")) multiplexer_6 (
    .in0(mem_wb_buffer_1_datain_2), .in1(mem_wb_buffer_1_addrout), .in2(pcext_1_out_2), .out(WBout),
    .sel(wbcontrol_1_mux));  // open: in3

  // Notes on the sheet:
  //   RX
  //   JALR B
  //   RX
endmodule

module Dual_Ported_Register_File (
  input  CLK,
  input  WrEN,
  input  [3:0] WrREGNO,
  input  [3:0] RdREGNO1,
  input  [3:0] RdREGNO2,
  input  [31:0] INPUT,
  output [31:0] OUT1,
  output [31:0] OUT2
);

  wire En_a0, En_a1, En_a2, En_a3, En_a4, En_at, En_fp, En_k0, En_ra, En_s0, En_s1, En_s2, En_s3, En_sp,
       En_v0;
  wire [31:0] a0, a1, a2, a3, a4, at, fp, k0, ra, s0, s1, s2, s3, sp, v0, zero;

  Decoder #(.select(4), .disabled(0)) decoder_1 (
    .out1(En_at), .out2(En_v0), .out3(En_a0), .out4(En_a1), .out5(En_a2), .out6(En_a3), .out7(En_a4),
    .out8(En_s0), .out9(En_s1), .out10(En_s2), .out11(En_s3), .out12(En_k0), .out13(En_sp), .out14(En_fp),
    .out15(En_ra), .sel(WrREGNO), .en(WrEN));  // open: out0
  Register #(.width(32)) u_zero (.D(INPUT), .en(1'b0), .Q(zero), .clk(CLK));  // open: clr
  Register #(.width(32)) u_at (.D(INPUT), .en(En_at), .Q(at), .clk(CLK));  // open: clr
  Register #(.width(32)) u_v0 (.D(INPUT), .en(En_v0), .Q(v0), .clk(CLK));  // open: clr
  Register #(.width(32)) u_a0 (.D(INPUT), .en(En_a0), .Q(a0), .clk(CLK));  // open: clr
  Register #(.width(32)) u_a1 (.D(INPUT), .en(En_a1), .Q(a1), .clk(CLK));  // open: clr
  Register #(.width(32)) u_a2 (.D(INPUT), .en(En_a2), .Q(a2), .clk(CLK));  // open: clr
  Register #(.width(32)) u_a3 (.D(INPUT), .en(En_a3), .Q(a3), .clk(CLK));  // open: clr
  Register #(.width(32)) u_a4 (.D(INPUT), .en(En_a4), .Q(a4), .clk(CLK));  // open: clr
  Multiplexer #(.select(4), .width(32), .disabled(0), .enable("false")) multiplexer_1 (
    .in0(zero), .in1(at), .in2(v0), .in3(a0), .in4(a1), .in5(a2), .in6(a3), .in7(a4), .in8(s0), .in9(s1),
    .in10(s2), .in11(s3), .in12(k0), .in13(sp), .in14(fp), .in15(ra), .out(OUT2), .sel(RdREGNO2));
  Register #(.width(32)) u_s0 (.D(INPUT), .en(En_s0), .Q(s0), .clk(CLK));  // open: clr
  Register #(.width(32)) u_s1 (.D(INPUT), .en(En_s1), .Q(s1), .clk(CLK));  // open: clr
  Register #(.width(32)) u_s2 (.D(INPUT), .en(En_s2), .Q(s2), .clk(CLK));  // open: clr
  Register #(.width(32)) u_s3 (.D(INPUT), .en(En_s3), .Q(s3), .clk(CLK));  // open: clr
  Register #(.width(32)) u_k0 (.D(INPUT), .en(En_k0), .Q(k0), .clk(CLK));  // open: clr
  Register #(.width(32)) u_sp (.D(INPUT), .en(En_sp), .Q(sp), .clk(CLK));  // open: clr
  Register #(.width(32)) u_fp (.D(INPUT), .en(En_fp), .Q(fp), .clk(CLK));  // open: clr
  Register #(.width(32)) u_ra (.D(INPUT), .en(En_ra), .Q(ra), .clk(CLK));  // open: clr
  Multiplexer #(.select(4), .width(32), .disabled(0), .enable("false")) multiplexer_2 (
    .in0(zero), .in1(at), .in2(v0), .in3(a0), .in4(a1), .in5(a2), .in6(a3), .in7(a4), .in8(s0), .in9(s1),
    .in10(s2), .in11(s3), .in12(k0), .in13(sp), .in14(fp), .in15(ra), .out(OUT1), .sel(RdREGNO1));

  // Notes on the sheet:
  //   DO NOT MODIFY THIS FILE
endmodule

module IF_IDRR_Buffer (
  input  [23:0] PC_1in,
  input  [31:0] IMin,
  input  CLK,
  input  CLR,
  input  Stall,
  output [23:0] PC_1out,
  output [31:0] IMout
);

  wire not_1_out;

  Register #(.width(24)) register_1 (.D(PC_1in), .en(not_1_out), .Q(PC_1out), .clk(CLK), .clr(CLR));
  Register #(.width(32)) register_2 (.D(IMin), .en(not_1_out), .Q(IMout), .clk(CLK), .clr(CLR));
  not not_1 (not_1_out, Stall);
endmodule

module IDRR_EX_Buffer (
  input  [23:0] PC_1,
  input  [31:0] Ain,
  input  [31:0] Bin,
  input  [31:0] SEXin,
  input  [3:0] OPin,
  input  [3:0] RXin,
  input  [3:0] RYin,
  input  CLK,
  input  CLR,
  input  in_10,
  output [23:0] PC_1out,
  output [31:0] Aout,
  output [31:0] Bout,
  output [31:0] SEXout,
  output [3:0] OPout,
  output [3:0] RXout,
  output [3:0] RYout
);

  wire not_1_out;
  wire [3:0] multiplexer_1_out, multiplexer_2_out, multiplexer_3_out, register_5_q, register_6_q,
       register_7_q;
  wire [23:0] multiplexer_4_out, register_1_q;
  wire [31:0] multiplexer_5_out, multiplexer_6_out, multiplexer_7_out, register_2_q, register_3_q,
       register_4_q;

  Multiplexer #(.width(4), .enable("false")) multiplexer_1 (
    .in0(OPin), .in1(4'b0000), .out(multiplexer_1_out), .sel(CLR));
  Multiplexer #(.width(4), .enable("false")) multiplexer_2 (
    .in0(RXin), .in1(4'b0000), .out(multiplexer_2_out), .sel(CLR));
  Multiplexer #(.width(4), .enable("false")) multiplexer_3 (
    .in0(RYin), .in1(4'b0000), .out(multiplexer_3_out), .sel(CLR));
  Multiplexer #(.width(24), .enable("false")) multiplexer_4 (
    .in0(PC_1), .in1({24{1'b0}}), .out(multiplexer_4_out), .sel(CLR));
  Multiplexer #(.width(32), .enable("false")) multiplexer_5 (
    .in0(Ain), .in1({32{1'b0}}), .out(multiplexer_5_out), .sel(CLR));
  Multiplexer #(.width(32), .enable("false")) multiplexer_6 (
    .in0(Bin), .in1({32{1'b0}}), .out(multiplexer_6_out), .sel(CLR));
  Multiplexer #(.width(32), .enable("false")) multiplexer_7 (
    .in0(SEXin), .in1({32{1'b0}}), .out(multiplexer_7_out), .sel(CLR));
  Register #(.width(24)) register_1 (.D(multiplexer_4_out), .en(not_1_out), .Q(register_1_q), .clk(CLK));  // open: clr
  Register #(.width(32)) register_2 (.D(multiplexer_5_out), .en(not_1_out), .Q(register_2_q), .clk(CLK));  // open: clr
  Register #(.width(32)) register_3 (.D(multiplexer_6_out), .en(not_1_out), .Q(register_3_q), .clk(CLK));  // open: clr
  Register #(.width(32)) register_4 (.D(multiplexer_7_out), .en(not_1_out), .Q(register_4_q), .clk(CLK));  // open: clr
  Register #(.width(4)) register_5 (.D(multiplexer_1_out), .Q(register_5_q), .clk(CLK));  // open: en, clr
  Register #(.width(4)) register_6 (.D(multiplexer_2_out), .en(not_1_out), .Q(register_6_q), .clk(CLK));  // open: clr
  Register #(.width(4)) register_7 (.D(multiplexer_3_out), .en(not_1_out), .Q(register_7_q), .clk(CLK));  // open: clr
  not not_1 (not_1_out, in_10);
  Multiplexer #(.width(24), .enable("false")) multiplexer_8 (
    .in0({24{1'b0}}), .in1(register_1_q), .out(PC_1out), .sel(not_1_out));
  Multiplexer #(.width(32), .enable("false")) multiplexer_9 (
    .in0({32{1'b0}}), .in1(register_2_q), .out(Aout), .sel(not_1_out));
  Multiplexer #(.width(32), .enable("false")) multiplexer_10 (
    .in0({32{1'b0}}), .in1(register_3_q), .out(Bout), .sel(not_1_out));
  Multiplexer #(.width(32), .enable("false")) multiplexer_11 (
    .in0({32{1'b0}}), .in1(register_4_q), .out(SEXout), .sel(not_1_out));
  Multiplexer #(.width(4), .enable("false")) multiplexer_12 (
    .in0(4'b0000), .in1(register_5_q), .out(OPout), .sel(not_1_out));
  Multiplexer #(.width(4), .enable("false")) multiplexer_13 (
    .in0(4'b0000), .in1(register_6_q), .out(RXout), .sel(not_1_out));
  Multiplexer #(.width(4), .enable("false")) multiplexer_14 (
    .in0(4'b0000), .in1(register_7_q), .out(RYout), .sel(not_1_out));
endmodule

module EX_MEM_Buffer (
  input  [23:0] ADDin,
  input  [31:0] ALUin,
  input  [31:0] DATAin,
  input  [3:0] OPin,
  input  [3:0] RXin,
  input  [3:0] RYin,
  input  [23:0] PC_1,
  input  CLK,
  output [23:0] ADDout,
  output [31:0] ALUout,
  output [31:0] DATAin_2,
  output [3:0] OPout,
  output [3:0] RXout,
  output [3:0] RYout,
  output [23:0] PC_1_2
);

  Register #(.width(24)) register_1 (.D(ADDin), .Q(ADDout), .clk(CLK));  // open: en, clr
  Register #(.width(32)) register_2 (.D(ALUin), .Q(ALUout), .clk(CLK));  // open: en, clr
  Register #(.width(32)) register_3 (.D(DATAin), .Q(DATAin_2), .clk(CLK));  // open: en, clr
  Register #(.width(4)) register_4 (.D(OPin), .Q(OPout), .clk(CLK));  // open: en, clr
  Register #(.width(4)) register_5 (.D(RXin), .Q(RXout), .clk(CLK));  // open: en, clr
  Register #(.width(4)) register_6 (.D(RYin), .Q(RYout), .clk(CLK));  // open: en, clr
  Register #(.width(24)) register_7 (.D(PC_1), .Q(PC_1_2), .clk(CLK));  // open: en, clr
endmodule

module MEM_WB_Buffer (
  input  [31:0] DATAin,
  input  [31:0] ADDRin,
  input  [3:0] OPin,
  input  [3:0] RXin,
  input  [3:0] RYin,
  input  [23:0] PC_1,
  input  CLK,
  output [31:0] DATAin_2,
  output [31:0] ADDRout,
  output [3:0] OPout,
  output [3:0] RXout,
  output [3:0] RYout,
  output [23:0] PC_1_2
);

  Register #(.width(32)) register_1 (.D(DATAin), .Q(DATAin_2), .clk(CLK));  // open: en, clr
  Register #(.width(32)) register_2 (.D(ADDRin), .Q(ADDRout), .clk(CLK));  // open: en, clr
  Register #(.width(4)) register_3 (.D(OPin), .Q(OPout), .clk(CLK));  // open: en, clr
  Register #(.width(4)) register_4 (.D(RXin), .Q(RXout), .clk(CLK));  // open: en, clr
  Register #(.width(4)) register_5 (.D(RYin), .Q(RYout), .clk(CLK));  // open: en, clr
  Register #(.width(24)) register_6 (.D(PC_1), .Q(PC_1_2), .clk(CLK));  // open: en, clr
endmodule

module ALU (
  input  [1:0] FUNC,
  input  [31:0] A,
  input  [31:0] B,
  output [31:0] OUT
);

  wire [31:0] adder_1_out, adder_2_out, nand_1_out, subtractor_1_out;

  Adder #(.width(32)) adder_1 (.a(A), .b(B), .out(adder_1_out), .cin(1'b0));  // open: cout
  assign nand_1_out = ~(A & B);  // NAND_Gate nand_1, 32 bits wide
  Subtractor #(.width(32)) subtractor_1 (.a(A), .b(B), .out(subtractor_1_out), .bin(1'b0));  // open: bout
  Adder #(.width(32)) adder_2 (.a(A), .b(B), .out(adder_2_out), .cin(1'b1));  // open: cout
  Multiplexer #(.select(2), .width(32), .disabled(0), .enable("false")) multiplexer_1 (
    .in0(adder_1_out), .in1(nand_1_out), .in2(subtractor_1_out), .in3(adder_2_out), .out(OUT), .sel(FUNC));

  // Notes on the sheet:
  //   DO NOT MODIFY THIS
endmodule

module SEXT (
  input  [31:0] Din,
  output [31:0] Dout
);


  assign Dout = {{13{Din[19]}}, Din[18:0]};
endmodule

module SRED (
  input  [31:0] Din,
  output [23:0] Dout
);


  assign Dout = Din[23:0];
endmodule

module IDRRControl (
  input  [3:0] RX,
  input  [3:0] RZ,
  input  [3:0] OPCode,
  output [3:0] RX_RZ
);

  Multiplexer #(.select(4), .width(4)) multiplexer_1 (
    .in0(RZ), .in1(RZ), .in2(RZ), .in3(RZ), .in4(RX), .in5(RX), .in6(RX), .out(RX_RZ), .sel(OPCode));  // open: in7, in8, in9, in10, in11, in12, in13, in14, in15, en
endmodule

module EXControl (
  input  [3:0] OPCode,
  output MUX,
  output [1:0] func
);

  Multiplexer #(.select(4)) multiplexer_1 (
    .in0(1'b0), .in1(1'b0), .in2(1'b1), .in3(1'b1), .in4(1'b1), .in5(1'b0), .in6(1'b0), .out(MUX),
    .sel(OPCode));  // open: in7, in8, in9, in10, in11, in12, in13, in14, in15, en
  Multiplexer #(.select(4), .width(2)) multiplexer_2 (
    .in0(2'b00), .in1(2'b01), .in2(2'b00), .in3(2'b00), .in4(2'b00), .in5(2'b10), .in6(2'b00), .out(func),
    .sel(OPCode));  // open: in7, in8, in9, in10, in11, in12, in13, in14, in15, en
endmodule

module MEMControl (
  input  [3:0] OPCode,
  output STR,
  output LD
);

  Multiplexer #(.select(4)) multiplexer_1 (
    .in0(1'b0), .in1(1'b0), .in2(1'b0), .in3(1'b0), .in4(1'b1), .in5(1'b0), .in6(1'b0), .in7(1'b0),
    .out(STR), .sel(OPCode));  // open: in8, in9, in10, in11, in12, in13, in14, in15, en
  Multiplexer #(.select(4)) multiplexer_2 (
    .in0(1'b0), .in1(1'b0), .in2(1'b0), .in3(1'b1), .in4(1'b0), .in5(1'b0), .in6(1'b0), .in7(1'b0), .out(LD),
    .sel(OPCode));  // open: in8, in9, in10, in11, in12, in13, in14, in15, en
endmodule

module WBControl (
  input  [3:0] OPCode,
  output WrEN,
  output [1:0] MUX,
  output RegMux
);

  Multiplexer #(.select(4)) multiplexer_1 (
    .in0(1'b1), .in1(1'b1), .in2(1'b1), .in3(1'b1), .in4(1'b0), .in5(1'b0), .in6(1'b0), .out(WrEN),
    .sel(OPCode));  // open: in7, in8, in9, in10, in11, in12, in13, in14, in15, en
  Multiplexer #(.select(4), .width(2)) multiplexer_2 (
    .in0(2'b01), .in1(2'b01), .in2(2'b01), .in3(2'b00), .in4(2'b00), .in5(2'b00), .in6(2'b10), .out(MUX),
    .sel(OPCode));  // open: in7, in8, in9, in10, in11, in12, in13, in14, in15, en
  Multiplexer #(.select(4)) multiplexer_3 (
    .in0(1'b0), .in1(1'b0), .in2(1'b0), .in3(1'b0), .in4(1'b0), .in5(1'b0), .in6(1'b1), .out(RegMux),
    .sel(OPCode));  // open: in7, in8, in9, in10, in11, in12, in13, in14, in15, en

  // Notes on the sheet:
  //   JALR store PC+1 into RY
  //   Or do we do that in ID/RR Stage
endmodule

module MUXBox (
  input  EQ,
  input  [3:0] OPCode,
  output [1:0] Sel,
  output FLUSH
);

  wire comparator_1_eq;

  or or_1 (FLUSH, Sel[0], Sel[1]);
  and and_1 (Sel[0], EQ, comparator_1_eq);
  Comparator #(.width(4)) comparator_1 (.a(4'b0101), .b(OPCode), .eq(comparator_1_eq));  // open: gt, lt
  Comparator #(.width(4)) comparator_2 (.a(OPCode), .b(4'b0110), .eq(Sel[1]));  // open: gt, lt
endmodule

module StallCheck (
  input  [3:0] OPCode,
  input  [3:0] RX,
  input  [3:0] RY,
  input  [3:0] RZ,
  input  [3:0] ID_RROP,
  input  [1:0] PCMux,
  output [1:0] PCMuxout,
  output Stall1,
  output Stall2
);

  wire and_1_out, and_2_out, and_3_out, comparator_1_gt, comparator_2_lt, comparator_3_eq, comparator_4_eq,
       comparator_5_eq;

  Multiplexer #(.width(2), .enable("false")) multiplexer_1 (.in0(PCMux), .in1(2'b11), .out(PCMuxout), .sel(Stall1));
  or or_1 (Stall1, and_1_out, and_2_out);
  and and_1 (and_1_out, comparator_3_eq, comparator_4_eq);
  and and_2 (and_2_out, comparator_3_eq, comparator_5_eq);
  and and_3 (and_3_out, comparator_1_gt, comparator_2_lt);
  Comparator #(.width(4)) comparator_1 (.a(4'b0110), .b(ID_RROP), .gt(comparator_1_gt));  // open: eq, lt
  Comparator #(.width(4)) comparator_2 (.a(4'b0001), .b(ID_RROP), .lt(comparator_2_lt));  // open: gt, eq
  Comparator #(.width(4)) comparator_3 (.a(4'b0011), .b(OPCode), .eq(comparator_3_eq));  // open: gt, lt
  Comparator #(.width(4)) comparator_4 (.a(RX), .b(RY), .eq(comparator_4_eq));  // open: gt, lt
  Comparator #(.width(4)) comparator_5 (.a(RX), .b(RZ), .eq(comparator_5_eq));  // open: gt, lt

  assign Stall2 = Stall1;

  // Notes on the sheet:
  //   EXE Stage
  //   ID/RR Stage
endmodule

module Forward_Circ (
  input  [3:0] RY,
  input  [3:0] RZorRX,
  input  [3:0] EXERx,
  input  [3:0] MEMRx,
  input  [31:0] ExeOut,
  input  [31:0] MemOut,
  input  [3:0] WBRx,
  input  [31:0] WBOut,
  output [1:0] out_9,
  output [1:0] out_10,
  output [31:0] FWRYOut,
  output [31:0] FWRZRXOut,
  output FY,
  output FZ
);

  wire comparator_3_eq, comparator_4_eq, comparator_5_eq, comparator_6_eq, comparator_7_eq, comparator_8_eq,
       FERY, FERZ, FMRY, FMRZ, FWRY, FWRZ, or_1_out, or_2_out, or_3_out, or_4_out;
  wire [1:0] multiplexer_3_out, multiplexer_4_out, multiplexer_5_out, multiplexer_6_out, multiplexer_7_out,
       multiplexer_8_out;

  Multiplexer #(.select(2), .width(32), .enable("false")) multiplexer_1 (
    .in0(ExeOut), .in1(MemOut), .in2(WBOut), .out(FWRYOut), .sel(out_10));  // open: in3
  Multiplexer #(.select(2), .width(32), .enable("false")) multiplexer_2 (
    .in0(ExeOut), .in1(MemOut), .in2(WBOut), .out(FWRZRXOut), .sel(out_9));  // open: in3
  Comparator #(.width(4)) comparator_1 (.a(RY), .b(EXERx), .eq(FERY));  // open: gt, lt
  Comparator #(.width(4)) comparator_2 (.a(RZorRX), .b(EXERx), .eq(FERZ));  // open: gt, lt
  or or_1 (or_1_out, FERY, FMRY, FWRY);
  Comparator #(.width(4)) comparator_3 (.a(RY), .b(4'b0000), .eq(comparator_3_eq));  // open: gt, lt
  Comparator #(.width(4)) comparator_4 (.a(RY), .b(MEMRx), .eq(comparator_4_eq));  // open: gt, lt
  Comparator #(.width(4)) comparator_5 (.a(MEMRx), .b(RZorRX), .eq(comparator_5_eq));  // open: gt, lt
  Comparator #(.width(4)) comparator_6 (.a(RY), .b(WBRx), .eq(comparator_6_eq));  // open: gt, lt
  Comparator #(.width(4)) comparator_7 (.a(WBRx), .b(RZorRX), .eq(comparator_7_eq));  // open: gt, lt
  and and_1 (FY, ~comparator_3_eq, or_1_out);  // AND_Gate
  Multiplexer #(.width(2), .enable("false")) multiplexer_3 (
    .in0(2'b00), .in1(2'b00), .out(multiplexer_3_out), .sel(FERY));
  and and_2 (FMRY, comparator_4_eq, ~FERY);  // AND_Gate
  and and_3 (FMRZ, comparator_5_eq, ~FERZ);  // AND_Gate
  or or_2 (or_2_out, FERZ, FMRZ, FWRZ);
  Multiplexer #(.width(2), .enable("false")) multiplexer_4 (
    .in0(2'b00), .in1(2'b00), .out(multiplexer_4_out), .sel(FERZ));
  or or_3 (or_3_out, FMRY, FERY);
  Comparator #(.width(4)) comparator_8 (.a(RZorRX), .b(4'b0000), .eq(comparator_8_eq));  // open: gt, lt
  or or_4 (or_4_out, FMRZ, FERZ);
  and and_4 (FZ, ~comparator_8_eq, or_2_out);  // AND_Gate
  Multiplexer #(.width(2), .enable("false")) multiplexer_5 (
    .in0(2'b00), .in1(2'b01), .out(multiplexer_5_out), .sel(FMRY));
  Multiplexer #(.width(2), .enable("false")) multiplexer_6 (
    .in0(2'b00), .in1(2'b01), .out(multiplexer_6_out), .sel(FMRZ));
  and and_5 (FWRY, comparator_6_eq, ~or_3_out);  // AND_Gate
  and and_6 (FWRZ, comparator_7_eq, ~or_4_out);  // AND_Gate
  Multiplexer #(.width(2), .enable("false")) multiplexer_7 (
    .in0(2'b00), .in1(2'b10), .out(multiplexer_7_out), .sel(FWRY));
  Multiplexer #(.width(2), .enable("false")) multiplexer_8 (
    .in0(2'b00), .in1(2'b10), .out(multiplexer_8_out), .sel(FWRZ));
  assign out_9 = multiplexer_4_out | multiplexer_6_out | multiplexer_8_out;  // OR_Gate or_5, 2 bits wide
  assign out_10 = multiplexer_3_out | multiplexer_5_out | multiplexer_7_out;  // OR_Gate or_6, 2 bits wide

  // Other names for the same wires on the sheet: RZ[3:0] = RZorRX; SelRXRZ[1:0] = out_9; SelRY[1:0] = out_10

  // Notes on the sheet:
  //   It is RX when: JALR, BEQ, and SW
  //   ID/RR
  //   Priorities
endmodule

module PCEXT (
  input  [23:0] PCin,
  output [31:0] out_2
);


  assign out_2 = {{8{1'b0}}, PCin};
endmodule
