// Logisim project lastname_firstname.circ as structural Verilog
module main (
);

  wire [7:0] adder_1_out;

  Multiplexer multiplexer_1 ();  // open: in0, in1, out, sel, en
  Adder adder_1 (.out(adder_1_out));  // open: a, b, cin, cout
endmodule

module Dual_Ported_Register_File (
  input  CLK,
  input  WrEN,
  input  [3:0] WrREGNO,
  input  [3:0] RdREGNO1,
  input  [3:0] RdREGNO2,
  input  [31:0] INPUT,
  output [31:0] OUT1,
  output [31:0] OUT2
);

  wire En_a0, En_a1, En_a2, En_a3, En_a4, En_at, En_fp, En_k0, En_ra, En_s0, En_s1, En_s2, En_s3, En_sp,
       En_v0;
  wire [31:0] a0, a1, a2, a3, a4, at, fp, k0, ra, s0, s1, s2, s3, sp, v0, zero;

  Decoder #(.select(4), .disabled(0)) decoder_1 (
    .out1(En_at), .out2(En_v0), .out3(En_a0), .out4(En_a1), .out5(En_a2), .out6(En_a3), .out7(En_a4),
    .out8(En_s0), .out9(En_s1), .out10(En_s2), .out11(En_s3), .out12(En_k0), .out13(En_sp), .out14(En_fp),
    .out15(En_ra), .sel(WrREGNO));  // open: out0, en
  Register #(.width(32)) u_zero (.D(INPUT), .en(1'b0), .Q(zero), .clk(CLK));  // open: clr
  Register #(.width(32)) u_at (.D(INPUT), .en(En_at), .Q(at), .clk(CLK));  // open: clr
  Register #(.width(32)) u_v0 (.D(INPUT), .en(En_v0), .Q(v0), .clk(CLK));  // open: clr
  Register #(.width(32)) u_a0 (.D(INPUT), .en(En_a0), .Q(a0), .clk(CLK));  // open: clr
  Register #(.width(32)) u_a1 (.D(INPUT), .en(En_a1), .Q(a1), .clk(CLK));  // open: clr
  Register #(.width(32)) u_a2 (.D(INPUT), .en(En_a2), .Q(a2), .clk(CLK));  // open: clr
  Register #(.width(32)) u_a3 (.D(INPUT), .en(En_a3), .Q(a3), .clk(CLK));  // open: clr
  Register #(.width(32)) u_a4 (.en(En_a4), .Q(a4), .clk(CLK));  // open: D, clr
  Multiplexer #(.select(4), .width(32), .disabled(0), .enable("false")) multiplexer_1 (
    .in0(zero), .in1(at), .in2(v0), .in3(a0), .in4(a1), .in5(a2), .in6(a3), .in7(a4), .in8(s0), .in9(s1),
    .in10(s2), .in11(s3), .in12(k0), .in13(sp), .in14(fp), .in15(ra), .out(OUT2), .sel(RdREGNO2));
  Register #(.width(32)) u_s0 (.D(INPUT), .en(En_s0), .Q(s0), .clk(CLK));  // open: clr
  Register #(.width(32)) u_s1 (.D(INPUT), .en(En_s1), .Q(s1), .clk(CLK));  // open: clr
  Register #(.width(32)) u_s2 (.D(INPUT), .en(En_s2), .Q(s2), .clk(CLK));  // open: clr
  Register #(.width(32)) u_s3 (.en(En_s3), .Q(s3), .clk(CLK));  // open: D, clr
  Register #(.width(32)) u_k0 (.D(INPUT), .en(En_k0), .Q(k0), .clk(CLK));  // open: clr
  Register #(.width(32)) u_sp (.D(INPUT), .en(En_sp), .Q(sp), .clk(CLK));  // open: clr
  Register #(.width(32)) u_fp (.D(INPUT), .en(En_fp), .Q(fp), .clk(CLK));  // open: clr
  Register #(.width(32)) u_ra (.en(En_ra), .Q(ra), .clk(CLK));  // open: D, clr
  Multiplexer #(.select(4), .width(32), .disabled(0), .enable("false")) multiplexer_2 (
    .in0(zero), .in1(at), .in2(v0), .in3(a0), .in4(a1), .in5(a2), .in6(a3), .in7(a4), .in8(s0), .in9(s1),
    .in10(s2), .in11(s3), .in12(k0), .in13(sp), .in14(fp), .in15(ra), .out(OUT1), .sel(RdREGNO1));

  // Notes on the sheet:
  //   DO NOT MODIFY THIS FILE
endmodule

module ALU (
  input  [1:0] FUNC,
  input  [31:0] A,
  input  [31:0] B,
  output [31:0] OUT
);

  wire [31:0] adder_1_out, adder_2_out, nand_1_out, subtractor_1_out;

  Adder #(.width(32)) adder_1 (.a(A), .b(B), .out(adder_1_out), .cin(1'b0));  // open: cout
  assign nand_1_out = ~(A & B);  // NAND_Gate nand_1, 32 bits wide
  Subtractor #(.width(32)) subtractor_1 (.a(A), .b(B), .out(subtractor_1_out), .bin(1'b0));  // open: bout
  Adder #(.width(32)) adder_2 (.a(A), .b(B), .out(adder_2_out), .cin(1'b1));  // open: cout
  Multiplexer #(.select(2), .width(32), .disabled(0), .enable("false")) multiplexer_1 (
    .in0(adder_1_out), .in1(nand_1_out), .in2(subtractor_1_out), .in3(adder_2_out), .out(OUT), .sel(FUNC));

  // Notes on the sheet:
  //   DO NOT MODIFY THIS
endmodule
